// Logisim project ALU.circ as structural Verilog: 10 circuits, main circuit full_adder_2bits
module main (
  input  in_1,
  input  [7:0] in_2,
  input  [7:0] in_3,
  input  [7:0] in_4,
  input  in_5,
  input  in_6,
  input  in_7,
  output out_8,
  output [7:0] out_9
);

  wire [7:0] full_adder_8bits_1_r, mayor_que_1_1_out_2;

  mayor_que_1 mayor_que_1_1 (.in_1(in_4), .out_2(mayor_que_1_1_out_2));
  full_adder_8bits full_adder_8bits_1 (.in_1(in_1), .B(in_2), .A(in_3), .R(full_adder_8bits_1_r), .out_5(out_8));
  mux_4x8_8 mux_4x8_8_1 (
    .in_1(full_adder_8bits_1_r), .in_8(mayor_que_1_1_out_2), .in_9(in_5), .in_10(in_6), .in_11(in_7),
    .out_12(out_9));  // open: in_2, in_3, in_4, in_5, in_6, in_7
endmodule

module mux_2x1_1 (
  input  A,
  input  B,
  input  in_3,
  output out_4
);

  wire and_1_out, and_2_out, not_1_out;

  not not_1 (not_1_out, in_3);
  and and_1 (and_1_out, A, not_1_out);
  and and_2 (and_2_out, B, in_3);
  or or_1 (out_4, and_1_out, and_2_out);
endmodule

module mux_4x1_1 (
  input  in_1,
  input  in_2,
  input  in_3,
  input  in_4,
  input  in_5,
  input  in_6,
  output out_7
);

  wire mux_2x1_1_1_out_4, mux_2x1_1_2_out_4;

  mux_2x1_1 mux_2x1_1_1 (.A(in_1), .B(in_2), .in_3(in_5), .out_4(mux_2x1_1_1_out_4));
  mux_2x1_1 mux_2x1_1_2 (.A(in_3), .B(in_4), .in_3(in_5), .out_4(mux_2x1_1_2_out_4));
  mux_2x1_1 mux_2x1_1_3 (.A(mux_2x1_1_1_out_4), .B(mux_2x1_1_2_out_4), .in_3(in_6), .out_4(out_7));
endmodule

module mux_8x1_1 (
  input  [7:0] in_1,
  input  in_2,
  input  in_3,
  input  in_4,
  output out_5
);

  wire mux_4x1_1_1_out_7, mux_4x1_1_2_out_7;

  mux_4x1_1 mux_4x1_1_1 (
    .in_1(in_1[0]), .in_2(in_1[4]), .in_3(in_1[2]), .in_4(in_1[6]), .in_5(in_2), .in_6(in_3),
    .out_7(mux_4x1_1_1_out_7));
  mux_4x1_1 mux_4x1_1_2 (
    .in_1(in_1[1]), .in_2(in_1[5]), .in_3(in_1[3]), .in_4(in_1[7]), .in_5(in_2), .in_6(in_3),
    .out_7(mux_4x1_1_2_out_7));
  mux_2x1_1 mux_2x1_1_1 (.A(mux_4x1_1_1_out_7), .B(mux_4x1_1_2_out_7), .in_3(in_4), .out_4(out_5));
endmodule

module half_adder (
  input  in_1,
  input  in_2,
  output out_3,
  output out_4
);

  xor xor_1 (out_3, in_1, in_2);
  and and_1 (out_4, in_1, in_2);
endmodule

module full_adder_2bits (
  input  A,
  input  B,
  input  Ci,
  output R,
  output C
);

  wire and_1_out, and_2_out, and_3_out, xor_1_out;

  xor xor_1 (xor_1_out, A, B);
  and and_1 (and_1_out, A, B);
  and and_2 (and_2_out, A, Ci);
  and and_3 (and_3_out, Ci, B);
  xor xor_2 (R, xor_1_out, Ci);
  or or_1 (C, and_1_out, and_2_out, and_3_out);
endmodule

module full_adder_8bits (
  input  in_1,
  input  [7:0] B,
  input  [7:0] A,
  output [7:0] R,
  output out_5
);

  wire full_adder_2bits_1_c, full_adder_2bits_2_c, full_adder_2bits_3_c, full_adder_2bits_4_c,
       full_adder_2bits_5_c, full_adder_2bits_6_c, full_adder_2bits_7_c;

  full_adder_2bits full_adder_2bits_1 (.A(A[0]), .B(B[0]), .R(R[0]), .C(full_adder_2bits_1_c), .Ci(in_1));
  full_adder_2bits full_adder_2bits_2 (
    .A(A[1]), .B(B[1]), .R(R[1]), .C(full_adder_2bits_2_c), .Ci(full_adder_2bits_1_c));
  full_adder_2bits full_adder_2bits_3 (
    .A(A[2]), .B(B[2]), .R(R[2]), .C(full_adder_2bits_3_c), .Ci(full_adder_2bits_2_c));
  full_adder_2bits full_adder_2bits_4 (
    .A(A[3]), .B(B[3]), .R(R[3]), .C(full_adder_2bits_4_c), .Ci(full_adder_2bits_3_c));
  full_adder_2bits full_adder_2bits_5 (
    .A(A[4]), .B(B[4]), .R(R[4]), .C(full_adder_2bits_5_c), .Ci(full_adder_2bits_4_c));
  full_adder_2bits full_adder_2bits_6 (
    .A(A[5]), .B(B[5]), .R(R[5]), .C(full_adder_2bits_6_c), .Ci(full_adder_2bits_5_c));
  full_adder_2bits full_adder_2bits_7 (
    .A(A[6]), .B(B[6]), .R(R[6]), .C(full_adder_2bits_7_c), .Ci(full_adder_2bits_6_c));
  full_adder_2bits full_adder_2bits_8 (.A(A[7]), .B(B[7]), .R(R[7]), .C(out_5), .Ci(full_adder_2bits_7_c));
endmodule

module mux_2x8_8 (
  input  [7:0] in_1,
  input  [7:0] in_2,
  input  in_3,
  output [7:0] out_4
);

  mux_2x1_1 mux_2x1_1_1 (.A(in_1[0]), .B(in_2[0]), .in_3(in_3), .out_4(out_4[0]));
  mux_2x1_1 mux_2x1_1_2 (.A(in_1[1]), .B(in_2[1]), .in_3(in_3), .out_4(out_4[1]));
  mux_2x1_1 mux_2x1_1_3 (.A(in_1[2]), .B(in_2[2]), .in_3(in_3), .out_4(out_4[2]));
  mux_2x1_1 mux_2x1_1_4 (.A(in_1[3]), .B(in_2[3]), .in_3(in_3), .out_4(out_4[3]));
  mux_2x1_1 mux_2x1_1_5 (.A(in_1[4]), .B(in_2[4]), .in_3(in_3), .out_4(out_4[4]));
  mux_2x1_1 mux_2x1_1_6 (.A(in_1[5]), .B(in_2[5]), .in_3(in_3), .out_4(out_4[5]));
  mux_2x1_1 mux_2x1_1_7 (.A(in_1[6]), .B(in_2[6]), .in_3(in_3), .out_4(out_4[6]));
  mux_2x1_1 mux_2x1_1_8 (.A(in_1[7]), .B(in_2[7]), .in_3(in_3), .out_4(out_4[7]));
endmodule

module mux_4x8_8 (
  input  [7:0] in_1,
  input  [7:0] in_2,
  input  [7:0] in_3,
  input  [7:0] in_4,
  input  [7:0] in_5,
  input  [7:0] in_6,
  input  [7:0] in_7,
  input  [7:0] in_8,
  input  in_9,
  input  in_10,
  input  in_11,
  output [7:0] out_12
);

  wire [7:0] mux_2x8_8_1_out_4, mux_2x8_8_2_out_4, mux_2x8_8_3_out_4, mux_2x8_8_4_out_4, mux_2x8_8_5_out_4,
       mux_2x8_8_6_out_4;

  mux_2x8_8 mux_2x8_8_1 (.in_1(in_1), .in_2(in_2), .out_4(mux_2x8_8_1_out_4), .in_3(in_11));
  mux_2x8_8 mux_2x8_8_2 (.in_1(in_3), .in_2(in_4), .out_4(mux_2x8_8_2_out_4), .in_3(in_11));
  mux_2x8_8 mux_2x8_8_3 (.in_1(in_5), .in_2(in_6), .out_4(mux_2x8_8_3_out_4), .in_3(in_11));
  mux_2x8_8 mux_2x8_8_4 (.in_1(in_7), .in_2(in_8), .out_4(mux_2x8_8_4_out_4), .in_3(in_11));
  mux_2x8_8 mux_2x8_8_5 (.in_1(mux_2x8_8_1_out_4), .in_2(mux_2x8_8_2_out_4), .out_4(mux_2x8_8_5_out_4), .in_3(in_10));
  mux_2x8_8 mux_2x8_8_6 (.in_1(mux_2x8_8_3_out_4), .in_2(mux_2x8_8_4_out_4), .out_4(mux_2x8_8_6_out_4), .in_3(in_10));
  mux_2x8_8 mux_2x8_8_7 (.in_1(mux_2x8_8_5_out_4), .in_2(mux_2x8_8_6_out_4), .out_4(out_12), .in_3(in_9));
endmodule

module mayor_que_1 (
  input  [7:0] in_1,
  output [7:0] out_2
);

  wire or_1_out, or_2_out, or_3_out, or_4_out, or_5_out, or_6_out;

  or or_1 (or_1_out, in_1[0], in_1[1]);
  or or_2 (or_2_out, in_1[2], in_1[3]);
  or or_3 (or_3_out, in_1[4], in_1[5]);
  or or_4 (or_4_out, in_1[6], in_1[7]);
  or or_5 (or_5_out, or_1_out, or_2_out);
  or or_6 (or_6_out, or_3_out, or_4_out);
  or or_7 (out_2[7], or_5_out, or_6_out);

  assign out_2[6:0] = {7{out_2[7]}};
endmodule
